# Fritzing sketch coeur de led fritzing (saved by Fritzing 0.9.3b)
breadboards: 1

parts:
  Composant1 = Arduino Uno (Rev3) - ICSP
  R1 = Resistor [tolerance=±5% resistance=220 package=THT]
  R2 = Resistor [tolerance=±5% resistance=220 package=THT]
  R3 = Resistor [tolerance=±5% resistance=220 package=THT]
  R4 = Resistor [tolerance=±5% resistance=220 package=THT]
  R5 = Resistor [tolerance=±5% resistance=220 package=THT]
  R6 = Resistor [tolerance=±5% resistance=220 package=THT]
  R7 = Resistor [tolerance=±5% resistance=220 package=THT]
  R8 = Resistor [tolerance=±5% resistance=220 package=THT]
  R9 = Resistor [tolerance=±5% resistance=220 package=THT]
  R10 = Resistor [tolerance=±5% resistance=220 package=THT]
  LED1 = LED - 5mm [color="Red (633nm)" package="5 mm [THT]"]
  LED2 = LED - 5mm [color="Red (633nm)" package="5 mm [THT]"]
  LED3 = LED - 5mm [color="Red (633nm)" package="5 mm [THT]"]
  LED4 = LED - 5mm [color="Red (633nm)" package="5 mm [THT]"]
  LED5 = LED - 5mm [color="Red (633nm)" package="5 mm [THT]"]
  LED6 = LED - 5mm [color="Red (633nm)" package="5 mm [THT]"]
  LED7 = LED - 5mm [color="Red (633nm)" package="5 mm [THT]"]
  LED8 = LED - 5mm [color="Red (633nm)" package="5 mm [THT]"]
  LED9 = LED - 5mm [color="Red (633nm)" package="5 mm [THT]"]
  LED10 = LED - 5mm [color="Red (633nm)" package="5 mm [THT]"]

nets:
  N1: Composant1.D8, LED7.anode
  N2: Composant1.D9_PWM, LED4.anode
  N3: Composant1.D10_PWM/SS, LED1.anode
  N4: Composant1.D1/TX, LED6.anode
  N5: Composant1.D2, LED3.anode
  N6: Composant1.D3_PWM, LED8.anode
  N7: Composant1.D4, LED5.anode
  N8: Composant1.D5_PWM, LED2.anode
  N9: Composant1.D6_PWM, LED9.anode
  N10: Composant1.D7, LED10.anode
  N11: Composant1.5V, R1.Pin_0, R2.Pin_0, R3.Pin_0, R4.Pin_0, R5.Pin_0, R6.Pin_0, R7.Pin_0, R8.Pin_0, R9.Pin_0, R10.Pin_0
  N12: R1.Pin_1, LED6.cathode
  N13: R2.Pin_1, LED3.cathode
  N14: R3.Pin_1, LED1.cathode
  N15: R4.Pin_1, LED2.cathode
  N16: R5.Pin_1, LED7.cathode
  N17: R6.Pin_1, LED9.cathode
  N18: R7.Pin_1, LED5.cathode
  N19: R8.Pin_1, LED8.cathode
  N20: R9.Pin_1, LED10.cathode
  N21: R10.Pin_1, LED4.cathode
